// Logisim project nova_memoria.circ as structural Verilog: 1 circuit, main circuit main
module main (
);

  wire undriven, undriven_2, undriven_3, undriven_4;

  D_Flip_Flop d_ff_1 (.D(undriven));  // open: clk, Q, Qn, preset, en, reset
  D_Flip_Flop d_ff_2 (.D(undriven));  // open: clk, Q, Qn, preset, en, reset
  D_Flip_Flop d_ff_3 (.D(undriven));  // open: clk, Q, Qn, preset, en, reset
  D_Flip_Flop d_ff_4 (.D(undriven));  // open: clk, Q, Qn, preset, en, reset
  D_Flip_Flop d_ff_5 (.D(undriven));  // open: clk, Q, Qn, preset, en, reset
  D_Flip_Flop d_ff_6 (.D(undriven));  // open: clk, Q, Qn, preset, en, reset
  D_Flip_Flop d_ff_7 (.D(undriven));  // open: clk, Q, Qn, preset, en, reset
  D_Flip_Flop d_ff_8 (.D(undriven));  // open: clk, Q, Qn, preset, en, reset
  D_Flip_Flop d_ff_9 (.D(undriven));  // open: clk, Q, Qn, preset, en, reset
  D_Flip_Flop d_ff_10 (.D(undriven));  // open: clk, Q, Qn, preset, en, reset
  D_Flip_Flop d_ff_11 (.D(undriven));  // open: clk, Q, Qn, preset, en, reset
  D_Flip_Flop d_ff_12 (.D(undriven));  // open: clk, Q, Qn, preset, en, reset
  D_Flip_Flop d_ff_13 (.D(undriven));  // open: clk, Q, Qn, preset, en, reset
  D_Flip_Flop d_ff_14 (.D(undriven));  // open: clk, Q, Qn, preset, en, reset
  D_Flip_Flop d_ff_15 (.D(undriven));  // open: clk, Q, Qn, preset, en, reset
  D_Flip_Flop d_ff_16 (.D(undriven));  // open: clk, Q, Qn, preset, en, reset
  D_Flip_Flop d_ff_17 (.D(undriven_2));  // open: clk, Q, Qn, preset, en, reset
  D_Flip_Flop d_ff_18 (.D(undriven_2));  // open: clk, Q, Qn, preset, en, reset
  D_Flip_Flop d_ff_19 (.D(undriven_2));  // open: clk, Q, Qn, preset, en, reset
  D_Flip_Flop d_ff_20 (.D(undriven_2));  // open: clk, Q, Qn, preset, en, reset
  D_Flip_Flop d_ff_21 (.D(undriven_2));  // open: clk, Q, Qn, preset, en, reset
  D_Flip_Flop d_ff_22 (.D(undriven_2));  // open: clk, Q, Qn, preset, en, reset
  D_Flip_Flop d_ff_23 (.D(undriven_2));  // open: clk, Q, Qn, preset, en, reset
  D_Flip_Flop d_ff_24 (.D(undriven_2));  // open: clk, Q, Qn, preset, en, reset
  D_Flip_Flop d_ff_25 (.D(undriven_2));  // open: clk, Q, Qn, preset, en, reset
  D_Flip_Flop d_ff_26 (.D(undriven_2));  // open: clk, Q, Qn, preset, en, reset
  D_Flip_Flop d_ff_27 (.D(undriven_2));  // open: clk, Q, Qn, preset, en, reset
  D_Flip_Flop d_ff_28 (.D(undriven_2));  // open: clk, Q, Qn, preset, en, reset
  D_Flip_Flop d_ff_29 (.D(undriven_2));  // open: clk, Q, Qn, preset, en, reset
  D_Flip_Flop d_ff_30 (.D(undriven_2));  // open: clk, Q, Qn, preset, en, reset
  D_Flip_Flop d_ff_31 (.D(undriven_2));  // open: clk, Q, Qn, preset, en, reset
  D_Flip_Flop d_ff_32 (.D(undriven_2));  // open: clk, Q, Qn, preset, en, reset
  D_Flip_Flop d_ff_33 (.D(undriven_3));  // open: clk, Q, Qn, preset, en, reset
  D_Flip_Flop d_ff_34 (.D(undriven_3));  // open: clk, Q, Qn, preset, en, reset
  D_Flip_Flop d_ff_35 (.D(undriven_3));  // open: clk, Q, Qn, preset, en, reset
  D_Flip_Flop d_ff_36 (.D(undriven_3));  // open: clk, Q, Qn, preset, en, reset
  D_Flip_Flop d_ff_37 (.D(undriven_3));  // open: clk, Q, Qn, preset, en, reset
  D_Flip_Flop d_ff_38 (.D(undriven_3));  // open: clk, Q, Qn, preset, en, reset
  D_Flip_Flop d_ff_39 (.D(undriven_3));  // open: clk, Q, Qn, preset, en, reset
  D_Flip_Flop d_ff_40 (.D(undriven_3));  // open: clk, Q, Qn, preset, en, reset
  D_Flip_Flop d_ff_41 (.D(undriven_3));  // open: clk, Q, Qn, preset, en, reset
  D_Flip_Flop d_ff_42 (.D(undriven_3));  // open: clk, Q, Qn, preset, en, reset
  D_Flip_Flop d_ff_43 (.D(undriven_3));  // open: clk, Q, Qn, preset, en, reset
  D_Flip_Flop d_ff_44 (.D(undriven_3));  // open: clk, Q, Qn, preset, en, reset
  D_Flip_Flop d_ff_45 (.D(undriven_3));  // open: clk, Q, Qn, preset, en, reset
  D_Flip_Flop d_ff_46 (.D(undriven_3));  // open: clk, Q, Qn, preset, en, reset
  D_Flip_Flop d_ff_47 (.D(undriven_3));  // open: clk, Q, Qn, preset, en, reset
  D_Flip_Flop d_ff_48 (.D(undriven_3));  // open: clk, Q, Qn, preset, en, reset
  D_Flip_Flop d_ff_49 (.D(undriven_4));  // open: clk, Q, Qn, preset, en, reset
  D_Flip_Flop d_ff_50 (.D(undriven_4));  // open: clk, Q, Qn, preset, en, reset
  D_Flip_Flop d_ff_51 (.D(undriven_4));  // open: clk, Q, Qn, preset, en, reset
  D_Flip_Flop d_ff_52 (.D(undriven_4));  // open: clk, Q, Qn, preset, en, reset
  D_Flip_Flop d_ff_53 (.D(undriven_4));  // open: clk, Q, Qn, preset, en, reset
  D_Flip_Flop d_ff_54 (.D(undriven_4));  // open: clk, Q, Qn, preset, en, reset
  D_Flip_Flop d_ff_55 (.D(undriven_4));  // open: clk, Q, Qn, preset, en, reset
  D_Flip_Flop d_ff_56 (.D(undriven_4));  // open: clk, Q, Qn, preset, en, reset
  D_Flip_Flop d_ff_57 (.D(undriven_4));  // open: clk, Q, Qn, preset, en, reset
  D_Flip_Flop d_ff_58 (.D(undriven_4));  // open: clk, Q, Qn, preset, en, reset
  D_Flip_Flop d_ff_59 (.D(undriven_4));  // open: clk, Q, Qn, preset, en, reset
  D_Flip_Flop d_ff_60 (.D(undriven_4));  // open: clk, Q, Qn, preset, en, reset
  D_Flip_Flop d_ff_61 (.D(undriven_4));  // open: clk, Q, Qn, preset, en, reset
  D_Flip_Flop d_ff_62 (.D(undriven_4));  // open: clk, Q, Qn, preset, en, reset
  D_Flip_Flop d_ff_63 (.D(undriven_4));  // open: clk, Q, Qn, preset, en, reset
  D_Flip_Flop d_ff_64 (.D(undriven_4));  // open: clk, Q, Qn, preset, en, reset
endmodule
